# Fritzing sketch ApproxyClock (saved by Fritzing 0.8.7b)
circuit board: 16cm x 10cm
breadboards: 1

parts:
  VCC1 = 4 x AAA Battery Mount
  A1 = atmega328 [package=dip]
  C2 = Capacitor [package=cap-pth-small2]
  C1 = Capacitor [package=cap-pth-small2]
  Y1 = CRYSTAL [package=crystal-smd-10.5x4.8-2pin]
  TL = Resistor [tolerance=±5% resistance=0 package=THT]  # not connected
  TR = Resistor [tolerance=±5% resistance=0 package=THT]  # not connected
  RRST = Resistor [tolerance=±5% resistance=10k package=THT]
  LED1 = RGB LED (com. cathode, rbg) [package="5 mm [THT]"]

nets:
  N1: VCC1.-, A1.GND, C2.2, C1.2, RRST.Pin_1, LED1.common_cathode
  N2: VCC1.+, A1.RESET, A1.VCC, A1.D7, A1.AVCC, A1.AREF, RRST.Pin_0
  N3: A1.D3_(PWM), LED1.blue_anode
  N4: A1.XLAT1, C1.1, Y1.1
  N5: A1.XLAT2, C2.1, Y1.2
  N6: A1.D5_(PWM), LED1.red_anode
  N7: A1.D6_(PWM), LED1.green_anode

notes:
  SN74HC595
  16 15 14 13 12 11 10 9
  | | | | | | | |
  +--+--+--+--+--+--+--+
  |> |
  +--+--+--+--+--+--+--+
  | | | | | | | |
  1 2 3 4 5 6 7 8
  Officiele pin namen:
  1: Q2
  2: Q3
  3: Q4
  3: Q5
  5: Q6
  6: Q7
  7: Q8
  8: GND
  9: QH* (voor daisy chaining)
  10: SRCLR* (naar 5V)
  11: SRCLK (naar D4): clock pin
  12: RCLK (naar D3): latch pin
  13: OE* (naar GND)
  14: SER (naar D2): data pin
  15: Q1
  16: VCC (naar 5V)
  Capacitors: 22 pF
  Crystal: 16 MHz
  RRST: Pull-up resistance for reset
